// Logisim project ALU.circ as structural Verilog: 3 circuits, main circuit main
module main (
  input  [2:0] Selection_Input,
  input  Cin_ADDER,
  input  [1:0] Input_A,
  input  [1:0] Input_B,
  output [1:0] Output
);

  wire full_adder_1_cout, full_adder_1_s, full_adder_2_s, full_adder_3_cout, full_adder_3_s, full_adder_4_s,
       n5_to_1_mulitplexer_1_iout0, n5_to_1_mulitplexer_1_iout1, n5_to_1_mulitplexer_1_iout2, nand_1_out,
       nand_2_out, not_1_out, not_2_out, xor_1_out, xor_2_out;

  Full_Adder full_adder_1 (
    .A(Input_A[0]), .B(Input_B[0]), .Cin(Cin_ADDER), .S(full_adder_1_s), .Cout(full_adder_1_cout));
  Full_Adder full_adder_2 (.A(Input_A[1]), .B(Input_B[1]), .Cin(full_adder_1_cout), .S(full_adder_2_s));  // open: Cout
  not not_1 (not_1_out, Input_A[0]);
  xor xor_1 (xor_1_out, Input_A[0], Input_B[0]);
  nand nand_1 (nand_1_out, Input_A[0], Input_B[0]);
  Full_Adder full_adder_3 (.A(Input_A[0]), .B(1'b1), .Cin(1'b0), .S(full_adder_3_s), .Cout(full_adder_3_cout));
  not not_2 (not_2_out, Input_A[1]);
  xor xor_2 (xor_2_out, Input_A[1], Input_B[1]);
  nand nand_2 (nand_2_out, Input_A[1], Input_B[1]);
  Full_Adder full_adder_4 (.A(Input_A[1]), .B(1'b0), .Cin(full_adder_3_cout), .S(full_adder_4_s));  // open: Cout
  _5_to_1_Mulitplexer u_5_to_1_mulitplexer_1 (
    .\Α (not_1_out), .\Β (full_adder_1_s), .C(xor_1_out), .D(nand_1_out), .E(full_adder_3_s), .O(Output[0]),
    .I2(Selection_Input[2]), .\Ι1 (Selection_Input[1]), .\Ι0 (Selection_Input[0]),
    .Iout2(n5_to_1_mulitplexer_1_iout2), .Iout0(n5_to_1_mulitplexer_1_iout0),
    .Iout1(n5_to_1_mulitplexer_1_iout1));
  _5_to_1_Mulitplexer u_5_to_1_mulitplexer_2 (
    .\Α (not_2_out), .\Β (full_adder_2_s), .C(xor_2_out), .D(nand_2_out), .E(full_adder_4_s), .O(Output[1]),
    .I2(n5_to_1_mulitplexer_1_iout2), .\Ι1 (n5_to_1_mulitplexer_1_iout1), .\Ι0 (n5_to_1_mulitplexer_1_iout0));  // open: Iout2, Iout0, Iout1

  // Notes on the sheet:
  //   000 - NOT_A
  //   001 - A+B
  //   010 - A XOR B
  //   011 - A NAND B
  //   100 - A+1
  //   (5 to 7 means nothing)
endmodule

// 5 to 1 MUX
module _5_to_1_Mulitplexer (
  input  I2,
  input  \Ι1 ,
  input  \Ι0 ,
  input  \Α ,
  input  \Β ,
  input  C,
  input  D,
  input  E,
  output O,
  output Iout2,
  output Iout1,
  output Iout0
);

  wire and_1_out, and_2_out, and_3_out, and_4_out, and_5_out, not_1_out, not_2_out, not_3_out, not_4_out,
       not_5_out, not_6_out, not_7_out, not_8_out, not_9_out, not_10_out;

  not not_1 (not_1_out, \Ι1 );
  not not_2 (not_2_out, \Ι1 );
  not not_3 (not_3_out, \Ι1 );
  not not_4 (not_4_out, \Ι0 );
  not not_5 (not_5_out, I2);
  not not_6 (not_6_out, I2);
  not not_7 (not_7_out, \Ι0 );
  not not_8 (not_8_out, I2);
  not not_9 (not_9_out, I2);
  not not_10 (not_10_out, \Ι0 );
  and and_1 (and_1_out, \Α , not_4_out, not_1_out, not_5_out);
  and and_2 (and_2_out, \Β , \Ι0 , not_2_out, not_6_out);
  and and_3 (and_3_out, C, not_7_out, \Ι1 , not_8_out);
  and and_4 (and_4_out, D, \Ι0 , \Ι1 , not_9_out);
  and and_5 (and_5_out, E, not_10_out, not_3_out, I2);
  or or_1 (O, and_1_out, and_2_out, and_3_out, and_4_out, and_5_out);

  assign Iout0 = \Ι0 ;
  assign Iout1 = \Ι1 ;
  assign Iout2 = I2;
endmodule

module Full_Adder (
  input  A,
  input  B,
  input  Cin,
  output S,
  output Cout
);

  wire and_1_out, and_2_out, xor_1_out;

  xor xor_1 (xor_1_out, A, B);
  and and_1 (and_1_out, A, B);
  xor xor_2 (S, xor_1_out, Cin);
  and and_2 (and_2_out, xor_1_out, Cin);
  or or_1 (Cout, and_2_out, and_1_out);
endmodule
