// Logisim project mod-9 sychronous J-K FF based up-counter.circ as structural Verilog: 4 circuits, main circuit main
module main (
  input  PRE,
  input  CLR,
  input  CTRL,
  output [3:0] Output
);

  wire and_1_out, and_2_out, and_3_out, and_4_out, and_5_out, CLK_out, not_1_out, or_1_out, or_2_out;

  Clock CLK (.out(CLK_out));
  and and_1 (and_1_out, CLK_out, CTRL);
  not not_1 (not_1_out, Output[3]);
  and and_2 (and_2_out, Output[0], not_1_out);
  or or_1 (or_1_out, Output[0], Output[3]);
  and and_3 (and_3_out, Output[1], Output[0], not_1_out);
  or or_2 (or_2_out, Output[3], and_4_out);
  and and_4 (and_4_out, Output[0], Output[1]);
  and and_5 (and_5_out, Output[2], Output[0], Output[1]);
  J_K_FF_Negative_Edge_Triggered j_k_ff_negative_edge_triggered_1 (
    .PRE(PRE), .J(not_1_out), .K(not_1_out), .CLK(and_1_out), .CLR(CLR), .Q(Output[0]));  // open: Q_prime
  J_K_FF_Negative_Edge_Triggered j_k_ff_negative_edge_triggered_2 (
    .PRE(PRE), .J(and_2_out), .K(or_1_out), .CLK(and_1_out), .CLR(CLR), .Q(Output[1]));  // open: Q_prime
  J_K_FF_Negative_Edge_Triggered j_k_ff_negative_edge_triggered_3 (
    .PRE(PRE), .J(and_3_out), .K(or_2_out), .CLK(and_1_out), .CLR(CLR), .Q(Output[2]));  // open: Q_prime
  J_K_FF_Negative_Edge_Triggered j_k_ff_negative_edge_triggered_4 (
    .PRE(PRE), .J(and_5_out), .K(Output[3]), .CLK(and_1_out), .CLR(CLR), .Q(Output[3]));  // open: Q_prime
endmodule

module D_Latch (
  input  D,
  input  PRE,
  input  EN,
  input  CLR,
  output Q,
  output Q_prime
);

  wire nand_1_out, nand_2_out, not_1_out;

  not not_1 (not_1_out, D);
  nand nand_1 (nand_1_out, D, EN);
  nand nand_2 (nand_2_out, EN, not_1_out);
  nand nand_3 (Q, PRE, nand_1_out, Q_prime);
  nand nand_4 (Q_prime, Q, nand_2_out, CLR);
endmodule

module D_FF_Negative_Edge_Triggered (
  input  PRE,
  input  D,
  input  CLK,
  input  CLR,
  output Q,
  output Q_prime
);

  wire d_latch_1_q, not_1_out;

  D_Latch d_latch_1 (.D(D), .PRE(PRE), .EN(CLK), .CLR(CLR), .Q(d_latch_1_q));  // open: Q_prime
  not not_1 (not_1_out, CLK);
  D_Latch d_latch_2 (.D(d_latch_1_q), .PRE(PRE), .EN(not_1_out), .CLR(CLR), .Q(Q), .Q_prime(Q_prime));
endmodule

module J_K_FF_Negative_Edge_Triggered (
  input  PRE,
  input  J,
  input  K,
  input  CLK,
  input  CLR,
  output Q,
  output Q_prime
);

  wire and_1_out, and_2_out, not_1_out, or_1_out;

  not not_1 (not_1_out, K);
  and and_1 (and_1_out, Q_prime, J);
  and and_2 (and_2_out, not_1_out, Q);
  or or_1 (or_1_out, and_1_out, and_2_out);
  D_FF_Negative_Edge_Triggered d_ff_negative_edge_triggered_1 (
    .PRE(PRE), .D(or_1_out), .CLK(CLK), .CLR(CLR), .Q(Q), .Q_prime(Q_prime));
endmodule
